// Logisim project CPUFinal_display_version.circ as structural Verilog: 7 circuits, main circuit main
module main (
  input  in_1,
  input  in_2,
  output [7:0] out_3,
  output [7:0] out_4
);

  wire alu32bit_1_zeroflag, alucontrol_1_sub, and_1_out, clock_1_out, clock_2_out, clock_3_out, clock_4_out,
       controlunit_1_aluopcon, controlunit_1_alusrc, controlunit_1_branch, controlunit_1_branchne,
       controlunit_1_jalr, controlunit_1_jr, controlunit_1_jump, controlunit_1_memread,
       controlunit_1_memtoreg, controlunit_1_memwrite, controlunit_1_regdest, controlunit_1_regwrite,
       controlunit_1_shiftco;
  wire [2:0] alucontrol_1_op;
  wire [3:0] controlunit_1_aluop;
  wire [4:0] multiplexer_1_out;
  wire [5:0] rom_1_data_2;
  wire [23:16] alu32bit_1_result;
  wire [25:0] rom_1_data;
  wire [31:0] bit_extender_1_out, multiplexer_2_out, multiplexer_3_out, multiplexer_4_out,
       pc_control_1_newpc, pc_control_1_pc4, ram_1_dout, register_1_q, registers_1_busa, registers_1_busb;
  wire [31:24] alu32bit_1_result_2;

  Register #(.width(32)) register_1 (
    .D(pc_control_1_newpc), .clk(clock_1_out), .Q(register_1_q), .clr(in_1));  // open: en
  Clock clock_1 (.out(clock_1_out));
  ROM #(.addrWidth(24), .dataWidth(32)) rom_1 (.addr(register_1_q[23:0]), .data({rom_1_data_2, rom_1_data}));
  Multiplexer #(.width(5)) multiplexer_1 (
    .in0(rom_1_data[20:16]), .in1(rom_1_data[15:11]), .out(multiplexer_1_out), .sel(controlunit_1_regdest));
  Clock clock_2 (.out(clock_2_out));
  assign bit_extender_1_out = {{16{rom_1_data[15]}}, rom_1_data[15:0]};  // Bit_Extender bit_extender_1
  ControlUnit controlunit_1 (
    .Op(rom_1_data_2), .func(rom_1_data[5:0]), .RegDest(controlunit_1_regdest), .Jump(controlunit_1_jump),
    .Branch(controlunit_1_branch), .BranchNE(controlunit_1_branchne), .MemRead(controlunit_1_memread),
    .MemToReg(controlunit_1_memtoreg), .MemWrite(controlunit_1_memwrite), .AlUSrc(controlunit_1_alusrc),
    .RegWrite(controlunit_1_regwrite), .AluOpCon(controlunit_1_aluopcon), .AluOp(controlunit_1_aluop),
    .jalr(controlunit_1_jalr), .ShiftCo(controlunit_1_shiftco), .jr(controlunit_1_jr));
  Registers registers_1 (
    .clk(clock_2_out), .Reset(in_2), .Rb(rom_1_data[20:16]), .Ra(rom_1_data[25:21]),
    .BusC(multiplexer_4_out), .Rw(multiplexer_1_out), .RegWrite(controlunit_1_regwrite),
    .BusB(registers_1_busb), .BusA(registers_1_busa));
  Multiplexer #(.width(32)) multiplexer_2 (
    .in0(registers_1_busb), .in1(bit_extender_1_out), .out(multiplexer_2_out), .sel(controlunit_1_alusrc));
  AluControl alucontrol_1 (
    .AluOPCon(controlunit_1_aluopcon), .ALUOP(controlunit_1_aluop), .Func(rom_1_data[5:0]),
    .Op(alucontrol_1_op), .Sub(alucontrol_1_sub));
  PC_Control pc_control_1 (
    .Jr(controlunit_1_jr), .Branch26(rom_1_data), .OldPC(register_1_q), .Immediate(bit_extender_1_out),
    .Jump(controlunit_1_jump), .Branch(controlunit_1_branch), .BranchNE(controlunit_1_branchne),
    .jalr(controlunit_1_jalr), .BusA(registers_1_busa), .ZeroFlag(alu32bit_1_zeroflag),
    .NewPC(pc_control_1_newpc), .PC4(pc_control_1_pc4));
  Alu32bit alu32bit_1 (
    .Sub(alucontrol_1_sub), .Op(alucontrol_1_op), .shamt(rom_1_data[10:6]), .ShiftCo(controlunit_1_shiftco),
    .B(multiplexer_2_out), .A(registers_1_busa), .ZeroFlag(alu32bit_1_zeroflag),
    .Result({alu32bit_1_result_2, alu32bit_1_result, out_4, out_3}));
  Clock clock_3 (.out(clock_3_out));
  RAM #(.addrWidth(24), .asyncread("true"), .dataWidth(32)) ram_1 (
    .addr({alu32bit_1_result, out_4, out_3}), .we(controlunit_1_memwrite), .oe(controlunit_1_memread),
    .clk(clock_3_out), .din(registers_1_busb), .dout(ram_1_dout));
  Multiplexer #(.width(32)) multiplexer_3 (
    .in0({alu32bit_1_result_2, alu32bit_1_result, out_4, out_3}), .in1(ram_1_dout), .out(multiplexer_3_out),
    .sel(controlunit_1_memtoreg));
  Multiplexer #(.width(32)) multiplexer_4 (
    .in0(multiplexer_3_out), .in1(pc_control_1_pc4), .out(multiplexer_4_out), .sel(controlunit_1_jalr));
  Clock clock_4 (.out(clock_4_out));
  and and_1 (and_1_out, controlunit_1_memread, 1'b1);
  // RGB_Video #(.cursor("No Cursor"), .height(256), .scale(1), .width(256)) rgb_video_1: pin names not known; wires that end beside it: clock_4_out, and_1_out, out_3, out_4, ram_1_dout[23:0]

  // Notes on the sheet:
  //   contents of rom_1 (hex, n*v repeats v):
  //   2009ffff 0 0 0 11280003 0 0 0 8d100000 0 0 0 21080001 0 0 0 8000001 0 0 0 8000005
endmodule

module Registers (
  input  [4:0] Ra,
  input  [4:0] Rb,
  input  clk,
  input  Reset,
  input  [4:0] Rw,
  input  [31:0] BusC,
  input  RegWrite,
  output [31:0] BusA,
  output [31:0] BusB
);

  wire and_1_out, and_2_out, and_3_out, and_4_out, and_5_out, and_6_out, and_7_out, and_8_out, and_9_out,
       and_10_out, and_11_out, and_12_out, and_13_out, and_14_out, and_15_out, and_16_out, and_17_out,
       and_18_out, and_19_out, and_20_out, and_21_out, and_22_out, and_23_out, and_24_out, and_25_out,
       and_26_out, and_27_out, and_28_out, and_29_out, and_30_out, and_31_out, and_32_out, decoder_1_out0,
       decoder_1_out1, decoder_1_out2, decoder_1_out3, decoder_1_out4, decoder_1_out5, decoder_1_out6,
       decoder_1_out7, decoder_1_out8, decoder_1_out9, decoder_1_out10, decoder_1_out11, decoder_1_out12,
       decoder_1_out13, decoder_1_out14, decoder_1_out15, decoder_1_out16, decoder_1_out17, decoder_1_out18,
       decoder_1_out19, decoder_1_out20, decoder_1_out21, decoder_1_out22, decoder_1_out23, decoder_1_out24,
       decoder_1_out25, decoder_1_out26, decoder_1_out27, decoder_1_out28, decoder_1_out29, decoder_1_out30,
       decoder_1_out31;
  wire [31:0] register_1_q, register_2_q, register_3_q, register_4_q, register_5_q, register_6_q,
       register_7_q, register_8_q, register_9_q, register_10_q, register_11_q, register_12_q, register_13_q,
       register_14_q, register_15_q, register_16_q, register_17_q, register_18_q, register_19_q,
       register_20_q, register_21_q, register_22_q, register_23_q, register_24_q, register_25_q,
       register_26_q, register_27_q, register_28_q, register_29_q, register_30_q, register_31_q,
       register_32_q;

  Multiplexer #(.select(5), .width(32)) multiplexer_1 (
    .in0(register_1_q), .in1(register_2_q), .in2(register_3_q), .in3(register_4_q), .in4(register_5_q),
    .in5(register_6_q), .in6(register_7_q), .in7(register_8_q), .in8(register_9_q), .in9(register_10_q),
    .in10(register_11_q), .in11(register_12_q), .in12(register_13_q), .in13(register_14_q),
    .in14(register_15_q), .in15(register_16_q), .in16(register_17_q), .in17(register_18_q),
    .in18(register_19_q), .in19(register_20_q), .in20(register_21_q), .in21(register_22_q),
    .in22(register_23_q), .in23(register_24_q), .in24(register_25_q), .in25(register_26_q),
    .in26(register_27_q), .in27(register_28_q), .in28(register_29_q), .in29(register_30_q),
    .in30(register_31_q), .in31(register_32_q), .out(BusA), .sel(Ra));
  Register #(.width(32)) register_1 (.D({32{1'b0}}), .en(and_1_out), .clk(clk), .Q(register_1_q), .clr(Reset));
  Register #(.width(32)) register_2 (.D(BusC), .en(and_2_out), .clk(clk), .Q(register_2_q), .clr(Reset));
  Register #(.width(32)) register_3 (.D(BusC), .en(and_3_out), .clk(clk), .Q(register_3_q), .clr(Reset));
  Register #(.width(32)) register_4 (.D(BusC), .en(and_4_out), .clk(clk), .Q(register_4_q), .clr(Reset));
  Register #(.width(32)) register_5 (.D(BusC), .en(and_5_out), .clk(clk), .Q(register_5_q), .clr(Reset));
  Register #(.width(32)) register_6 (.D(BusC), .en(and_6_out), .clk(clk), .Q(register_6_q), .clr(Reset));
  Register #(.width(32)) register_7 (.D(BusC), .en(and_7_out), .clk(clk), .Q(register_7_q), .clr(Reset));
  Register #(.width(32)) register_8 (.D(BusC), .en(and_8_out), .clk(clk), .Q(register_8_q), .clr(Reset));
  and and_1 (and_1_out, decoder_1_out0, RegWrite);
  and and_2 (and_2_out, decoder_1_out1, RegWrite);
  and and_3 (and_3_out, decoder_1_out2, RegWrite);
  and and_4 (and_4_out, decoder_1_out3, RegWrite);
  and and_5 (and_5_out, decoder_1_out4, RegWrite);
  and and_6 (and_6_out, decoder_1_out5, RegWrite);
  and and_7 (and_7_out, decoder_1_out6, RegWrite);
  and and_8 (and_8_out, decoder_1_out7, RegWrite);
  and and_9 (and_9_out, decoder_1_out8, RegWrite);
  and and_10 (and_10_out, decoder_1_out9, RegWrite);
  and and_11 (and_11_out, decoder_1_out10, RegWrite);
  and and_12 (and_12_out, decoder_1_out11, RegWrite);
  and and_13 (and_13_out, decoder_1_out12, RegWrite);
  and and_14 (and_14_out, decoder_1_out13, RegWrite);
  and and_15 (and_15_out, decoder_1_out14, RegWrite);
  and and_16 (and_16_out, decoder_1_out15, RegWrite);
  Register #(.width(32)) register_9 (.D(BusC), .en(and_9_out), .clk(clk), .Q(register_9_q), .clr(Reset));
  Register #(.width(32)) register_10 (.D(BusC), .en(and_10_out), .clk(clk), .Q(register_10_q), .clr(Reset));
  Register #(.width(32)) register_11 (.D(BusC), .en(and_11_out), .clk(clk), .Q(register_11_q), .clr(Reset));
  Register #(.width(32)) register_12 (.D(BusC), .en(and_12_out), .clk(clk), .Q(register_12_q), .clr(Reset));
  Decoder #(.select(5)) decoder_1 (
    .out0(decoder_1_out0), .out1(decoder_1_out1), .out2(decoder_1_out2), .out3(decoder_1_out3),
    .out4(decoder_1_out4), .out5(decoder_1_out5), .out6(decoder_1_out6), .out7(decoder_1_out7),
    .out8(decoder_1_out8), .out9(decoder_1_out9), .out10(decoder_1_out10), .out11(decoder_1_out11),
    .out12(decoder_1_out12), .out13(decoder_1_out13), .out14(decoder_1_out14), .out15(decoder_1_out15),
    .out16(decoder_1_out16), .out17(decoder_1_out17), .out18(decoder_1_out18), .out19(decoder_1_out19),
    .out20(decoder_1_out20), .out21(decoder_1_out21), .out22(decoder_1_out22), .out23(decoder_1_out23),
    .out24(decoder_1_out24), .out25(decoder_1_out25), .out26(decoder_1_out26), .out27(decoder_1_out27),
    .out28(decoder_1_out28), .out29(decoder_1_out29), .out30(decoder_1_out30), .out31(decoder_1_out31),
    .sel(Rw));  // open: en
  Register #(.width(32)) register_13 (.D(BusC), .en(and_13_out), .clk(clk), .Q(register_13_q), .clr(Reset));
  Register #(.width(32)) register_14 (.D(BusC), .en(and_14_out), .clk(clk), .Q(register_14_q), .clr(Reset));
  Register #(.width(32)) register_15 (.D(BusC), .en(and_15_out), .clk(clk), .Q(register_15_q), .clr(Reset));
  Register #(.width(32)) register_16 (.D(BusC), .en(and_16_out), .clk(clk), .Q(register_16_q), .clr(Reset));
  Register #(.width(32)) register_17 (.D(BusC), .en(and_32_out), .clk(clk), .Q(register_17_q), .clr(Reset));
  Register #(.width(32)) register_18 (.D(BusC), .en(and_31_out), .clk(clk), .Q(register_18_q), .clr(Reset));
  Register #(.width(32)) register_19 (.D(BusC), .en(and_30_out), .clk(clk), .Q(register_19_q), .clr(Reset));
  Register #(.width(32)) register_20 (.D(BusC), .en(and_29_out), .clk(clk), .Q(register_20_q), .clr(Reset));
  Register #(.width(32)) register_21 (.D(BusC), .en(and_28_out), .clk(clk), .Q(register_21_q), .clr(Reset));
  Register #(.width(32)) register_22 (.D(BusC), .en(and_27_out), .clk(clk), .Q(register_22_q), .clr(Reset));
  Register #(.width(32)) register_23 (.D(BusC), .en(and_26_out), .clk(clk), .Q(register_23_q), .clr(Reset));
  Register #(.width(32)) register_24 (.D(BusC), .en(and_25_out), .clk(clk), .Q(register_24_q), .clr(Reset));
  and and_17 (and_17_out, decoder_1_out31, RegWrite);
  and and_18 (and_18_out, decoder_1_out30, RegWrite);
  and and_19 (and_19_out, decoder_1_out29, RegWrite);
  and and_20 (and_20_out, decoder_1_out28, RegWrite);
  and and_21 (and_21_out, decoder_1_out27, RegWrite);
  and and_22 (and_22_out, decoder_1_out26, RegWrite);
  and and_23 (and_23_out, decoder_1_out25, RegWrite);
  and and_24 (and_24_out, decoder_1_out24, RegWrite);
  and and_25 (and_25_out, decoder_1_out23, RegWrite);
  and and_26 (and_26_out, decoder_1_out22, RegWrite);
  and and_27 (and_27_out, decoder_1_out21, RegWrite);
  and and_28 (and_28_out, decoder_1_out20, RegWrite);
  and and_29 (and_29_out, decoder_1_out19, RegWrite);
  and and_30 (and_30_out, decoder_1_out18, RegWrite);
  and and_31 (and_31_out, decoder_1_out17, RegWrite);
  and and_32 (and_32_out, decoder_1_out16, RegWrite);
  Register #(.width(32)) register_25 (.D(BusC), .en(and_24_out), .clk(clk), .Q(register_25_q), .clr(Reset));
  Register #(.width(32)) register_26 (.D(BusC), .en(and_23_out), .clk(clk), .Q(register_26_q), .clr(Reset));
  Register #(.width(32)) register_27 (.D(BusC), .en(and_22_out), .clk(clk), .Q(register_27_q), .clr(Reset));
  Register #(.width(32)) register_28 (.D(BusC), .en(and_21_out), .clk(clk), .Q(register_28_q), .clr(Reset));
  Register #(.width(32)) register_29 (.D(BusC), .en(and_20_out), .clk(clk), .Q(register_29_q), .clr(Reset));
  Register #(.width(32)) register_30 (.D(BusC), .en(and_19_out), .clk(clk), .Q(register_30_q), .clr(Reset));
  Register #(.width(32)) register_31 (.D(BusC), .en(and_18_out), .clk(clk), .Q(register_31_q), .clr(Reset));
  Register #(.width(32)) register_32 (.D(BusC), .en(and_17_out), .clk(clk), .Q(register_32_q), .clr(Reset));
  Multiplexer #(.select(5), .width(32)) multiplexer_2 (
    .in0(register_1_q), .in1(register_2_q), .in2(register_3_q), .in3(register_4_q), .in4(register_5_q),
    .in5(register_6_q), .in6(register_7_q), .in7(register_8_q), .in8(register_9_q), .in9(register_10_q),
    .in10(register_11_q), .in11(register_12_q), .in12(register_13_q), .in13(register_14_q),
    .in14(register_15_q), .in15(register_16_q), .in16(register_17_q), .in17(register_18_q),
    .in18(register_19_q), .in19(register_20_q), .in20(register_21_q), .in21(register_22_q),
    .in22(register_23_q), .in23(register_24_q), .in24(register_25_q), .in25(register_26_q),
    .in26(register_27_q), .in27(register_28_q), .in28(register_29_q), .in29(register_30_q),
    .in30(register_31_q), .in31(register_32_q), .out(BusB), .sel(Rb));
endmodule

module ALU1Bit (
  input  Sub,
  input  Cin,
  input  A,
  input  B,
  input  [2:0] OP,
  input  Less,
  output Result,
  output Set,
  output Cout
);

  wire and_1_out, nor_1_out, or_1_out, xor_1_out, xor_2_out;

  xor xor_1 (xor_1_out, B, Sub);
  Adder #(.width(1)) adder_1 (.a(A), .b(xor_1_out), .out(Set), .cin(Cin), .cout(Cout));
  and and_1 (and_1_out, A, B);
  or or_1 (or_1_out, A, B);
  xor xor_2 (xor_2_out, A, B);
  nor nor_1 (nor_1_out, A, B);
  Multiplexer #(.select(3)) multiplexer_1 (
    .in0(and_1_out), .in1(or_1_out), .in2(Set), .in3(xor_2_out), .in4(nor_1_out), .in7(Less), .out(Result),
    .sel(OP));  // open: in5, in6
endmodule

module Alu32bit (
  input  Sub,
  input  [2:0] Op,
  input  [31:0] A,
  input  [31:0] B,
  input  [4:0] shamt,
  input  ShiftCo,
  output [31:0] Result,
  output ZeroFlag
);

  wire alu1bit_1_cout, alu1bit_2_cout, alu1bit_3_cout, alu1bit_4_cout, alu1bit_5_cout, alu1bit_6_cout,
       alu1bit_7_cout, alu1bit_8_cout, alu1bit_9_cout, alu1bit_10_cout, alu1bit_11_cout, alu1bit_12_cout,
       alu1bit_13_cout, alu1bit_14_cout, alu1bit_15_cout, alu1bit_16_cout, alu1bit_17_cout, alu1bit_18_cout,
       alu1bit_19_cout, alu1bit_20_cout, alu1bit_21_cout, alu1bit_22_cout, alu1bit_23_cout, alu1bit_24_cout,
       alu1bit_25_cout, alu1bit_26_cout, alu1bit_27_cout, alu1bit_28_cout, alu1bit_29_cout, alu1bit_30_cout,
       alu1bit_31_cout, alu1bit_32_set;
  wire [31:0] alu1bit_1_result, multiplexer_1_out, shifter_1_out, shifter_2_out, shifter_3_out,
       shifter_4_out, shifter_5_out, shifter_6_out;

  Shifter #(.width(32)) shifter_1 (.in(B), .\dist (shamt), .out(shifter_1_out));
  Shifter #(.shift("lr"), .width(32)) shifter_2 (.in(B), .\dist (shamt), .out(shifter_2_out));
  Shifter #(.shift("ar"), .width(32)) shifter_3 (.in(B), .\dist (shamt), .out(shifter_3_out));
  Shifter #(.width(32)) shifter_4 (.in(B), .\dist (A[4:0]), .out(shifter_4_out));
  Shifter #(.shift("lr"), .width(32)) shifter_5 (.in(B), .\dist (A[4:0]), .out(shifter_5_out));
  Shifter #(.width(32)) shifter_6 (.in(B), .\dist (A[4:0]), .out(shifter_6_out));
  ALU1Bit alu1bit_1 (
    .OP(Op), .A(A[0]), .B(B[0]), .Sub(Sub), .Cin(Sub), .Less(alu1bit_32_set), .Result(alu1bit_1_result[0]),
    .Cout(alu1bit_1_cout));  // open: Set
  ALU1Bit alu1bit_2 (
    .OP(Op), .A(A[1]), .B(B[1]), .Sub(Sub), .Cin(alu1bit_1_cout), .Less(1'b0), .Result(alu1bit_1_result[1]),
    .Cout(alu1bit_2_cout));  // open: Set
  ALU1Bit alu1bit_3 (
    .OP(Op), .A(A[2]), .B(B[2]), .Sub(Sub), .Cin(alu1bit_2_cout), .Less(1'b0), .Result(alu1bit_1_result[2]),
    .Cout(alu1bit_3_cout));  // open: Set
  ALU1Bit alu1bit_4 (
    .OP(Op), .A(A[3]), .B(B[3]), .Sub(Sub), .Cin(alu1bit_3_cout), .Less(1'b0), .Result(alu1bit_1_result[3]),
    .Cout(alu1bit_4_cout));  // open: Set
  ALU1Bit alu1bit_5 (
    .OP(Op), .A(A[4]), .B(B[4]), .Sub(Sub), .Cin(alu1bit_4_cout), .Less(1'b0), .Result(alu1bit_1_result[4]),
    .Cout(alu1bit_5_cout));  // open: Set
  ALU1Bit alu1bit_6 (
    .OP(Op), .A(A[5]), .B(B[5]), .Sub(Sub), .Cin(alu1bit_5_cout), .Less(1'b0), .Result(alu1bit_1_result[5]),
    .Cout(alu1bit_6_cout));  // open: Set
  ALU1Bit alu1bit_7 (
    .OP(Op), .A(A[6]), .B(B[6]), .Sub(Sub), .Cin(alu1bit_6_cout), .Less(1'b0), .Result(alu1bit_1_result[6]),
    .Cout(alu1bit_7_cout));  // open: Set
  ALU1Bit alu1bit_8 (
    .OP(Op), .A(A[7]), .B(B[7]), .Sub(Sub), .Cin(alu1bit_7_cout), .Less(1'b0), .Result(alu1bit_1_result[7]),
    .Cout(alu1bit_8_cout));  // open: Set
  Multiplexer #(.select(3), .width(32)) multiplexer_1 (
    .in0(shifter_1_out), .in2(shifter_2_out), .in3(shifter_3_out), .in4(shifter_4_out), .in6(shifter_5_out),
    .in7(shifter_6_out), .out(multiplexer_1_out), .sel(Op));  // open: in1, in5
  ALU1Bit alu1bit_9 (
    .OP(Op), .A(A[8]), .B(B[8]), .Sub(Sub), .Cin(alu1bit_8_cout), .Less(1'b0), .Result(alu1bit_1_result[8]),
    .Cout(alu1bit_9_cout));  // open: Set
  ALU1Bit alu1bit_10 (
    .OP(Op), .A(A[9]), .B(B[9]), .Sub(Sub), .Cin(alu1bit_9_cout), .Less(1'b0), .Result(alu1bit_1_result[9]),
    .Cout(alu1bit_10_cout));  // open: Set
  ALU1Bit alu1bit_11 (
    .OP(Op), .A(A[10]), .B(B[10]), .Sub(Sub), .Cin(alu1bit_10_cout), .Less(1'b0),
    .Result(alu1bit_1_result[10]), .Cout(alu1bit_11_cout));  // open: Set
  ALU1Bit alu1bit_12 (
    .OP(Op), .A(A[11]), .B(B[11]), .Sub(Sub), .Cin(alu1bit_11_cout), .Less(1'b0),
    .Result(alu1bit_1_result[11]), .Cout(alu1bit_12_cout));  // open: Set
  ALU1Bit alu1bit_13 (
    .OP(Op), .A(A[12]), .B(B[12]), .Sub(Sub), .Cin(alu1bit_12_cout), .Less(1'b0),
    .Result(alu1bit_1_result[12]), .Cout(alu1bit_13_cout));  // open: Set
  ALU1Bit alu1bit_14 (
    .OP(Op), .A(A[13]), .B(B[13]), .Sub(Sub), .Cin(alu1bit_13_cout), .Less(1'b0),
    .Result(alu1bit_1_result[13]), .Cout(alu1bit_14_cout));  // open: Set
  ALU1Bit alu1bit_15 (
    .OP(Op), .A(A[14]), .B(B[14]), .Sub(Sub), .Cin(alu1bit_14_cout), .Less(1'b0),
    .Result(alu1bit_1_result[14]), .Cout(alu1bit_15_cout));  // open: Set
  ALU1Bit alu1bit_16 (
    .OP(Op), .A(A[15]), .B(B[15]), .Sub(Sub), .Cin(alu1bit_15_cout), .Less(1'b0),
    .Result(alu1bit_1_result[15]), .Cout(alu1bit_16_cout));  // open: Set
  ALU1Bit alu1bit_17 (
    .OP(Op), .A(A[16]), .B(B[16]), .Sub(Sub), .Cin(alu1bit_16_cout), .Less(1'b0),
    .Result(alu1bit_1_result[16]), .Cout(alu1bit_17_cout));  // open: Set
  ALU1Bit alu1bit_18 (
    .OP(Op), .A(A[17]), .B(B[17]), .Sub(Sub), .Cin(alu1bit_17_cout), .Less(1'b0),
    .Result(alu1bit_1_result[17]), .Cout(alu1bit_18_cout));  // open: Set
  ALU1Bit alu1bit_19 (
    .OP(Op), .A(A[18]), .B(B[18]), .Sub(Sub), .Cin(alu1bit_18_cout), .Less(1'b0),
    .Result(alu1bit_1_result[18]), .Cout(alu1bit_19_cout));  // open: Set
  ALU1Bit alu1bit_20 (
    .OP(Op), .A(A[19]), .B(B[19]), .Sub(Sub), .Cin(alu1bit_19_cout), .Less(1'b0),
    .Result(alu1bit_1_result[19]), .Cout(alu1bit_20_cout));  // open: Set
  ALU1Bit alu1bit_21 (
    .OP(Op), .A(A[20]), .B(B[20]), .Sub(Sub), .Cin(alu1bit_20_cout), .Less(1'b0),
    .Result(alu1bit_1_result[20]), .Cout(alu1bit_21_cout));  // open: Set
  ALU1Bit alu1bit_22 (
    .OP(Op), .A(A[21]), .B(B[21]), .Sub(Sub), .Cin(alu1bit_21_cout), .Less(1'b0),
    .Result(alu1bit_1_result[21]), .Cout(alu1bit_22_cout));  // open: Set
  ALU1Bit alu1bit_23 (
    .OP(Op), .A(A[22]), .B(B[22]), .Sub(Sub), .Cin(alu1bit_22_cout), .Less(1'b0),
    .Result(alu1bit_1_result[22]), .Cout(alu1bit_23_cout));  // open: Set
  ALU1Bit alu1bit_24 (
    .OP(Op), .A(A[23]), .B(B[23]), .Sub(Sub), .Cin(alu1bit_23_cout), .Result(alu1bit_1_result[23]),
    .Cout(alu1bit_24_cout));  // open: Less, Set
  ALU1Bit alu1bit_25 (
    .OP(Op), .A(A[24]), .B(B[24]), .Sub(Sub), .Cin(alu1bit_24_cout), .Less(1'b0),
    .Result(alu1bit_1_result[31]), .Cout(alu1bit_25_cout));  // open: Set
  ALU1Bit alu1bit_26 (
    .OP(Op), .A(A[25]), .B(B[25]), .Sub(Sub), .Cin(alu1bit_25_cout), .Less(1'b0),
    .Result(alu1bit_1_result[30]), .Cout(alu1bit_26_cout));  // open: Set
  ALU1Bit alu1bit_27 (
    .OP(Op), .A(A[26]), .B(B[26]), .Sub(Sub), .Cin(alu1bit_26_cout), .Less(1'b0),
    .Result(alu1bit_1_result[29]), .Cout(alu1bit_27_cout));  // open: Set
  ALU1Bit alu1bit_28 (
    .OP(Op), .A(A[27]), .B(B[27]), .Sub(Sub), .Cin(alu1bit_27_cout), .Less(1'b0),
    .Result(alu1bit_1_result[28]), .Cout(alu1bit_28_cout));  // open: Set
  ALU1Bit alu1bit_29 (
    .OP(Op), .A(A[28]), .B(B[28]), .Sub(Sub), .Cin(alu1bit_28_cout), .Less(1'b0),
    .Result(alu1bit_1_result[27]), .Cout(alu1bit_29_cout));  // open: Set
  ALU1Bit alu1bit_30 (
    .OP(Op), .A(A[29]), .B(B[29]), .Sub(Sub), .Cin(alu1bit_29_cout), .Less(1'b0),
    .Result(alu1bit_1_result[26]), .Cout(alu1bit_30_cout));  // open: Set
  ALU1Bit alu1bit_31 (
    .OP(Op), .A(A[30]), .B(B[30]), .Sub(Sub), .Cin(alu1bit_30_cout), .Less(1'b0),
    .Result(alu1bit_1_result[25]), .Cout(alu1bit_31_cout));  // open: Set
  ALU1Bit alu1bit_32 (
    .OP(Op), .A(A[31]), .B(B[31]), .Sub(Sub), .Cin(alu1bit_31_cout), .Less(1'b0),
    .Result(alu1bit_1_result[24]), .Set(alu1bit_32_set));  // open: Cout
  nor nor_1 (ZeroFlag, alu1bit_1_result[31], alu1bit_1_result[30], alu1bit_1_result[29], alu1bit_1_result[28], alu1bit_1_result[27], alu1bit_1_result[26], alu1bit_1_result[25], alu1bit_1_result[24], alu1bit_1_result[23], alu1bit_1_result[22], alu1bit_1_result[21], alu1bit_1_result[20], alu1bit_1_result[19], alu1bit_1_result[18], alu1bit_1_result[17], alu1bit_1_result[16], alu1bit_1_result[15], alu1bit_1_result[14], alu1bit_1_result[13], alu1bit_1_result[12], alu1bit_1_result[11], alu1bit_1_result[10], alu1bit_1_result[9], alu1bit_1_result[8], alu1bit_1_result[7], alu1bit_1_result[6], alu1bit_1_result[5], alu1bit_1_result[4], alu1bit_1_result[3], alu1bit_1_result[2], alu1bit_1_result[1], alu1bit_1_result[0]);
  Multiplexer #(.width(32)) multiplexer_2 (
    .in0(alu1bit_1_result), .in1(multiplexer_1_out), .out(Result), .sel(ShiftCo));
endmodule

module AluControl (
  input  AluOPCon,
  input  [3:0] ALUOP,
  input  [5:0] Func,
  output [2:0] Op,
  output Sub
);

  wire and_1_out, and_2_out, and_3_out, and_4_out, nor_1_out, priority_encoder_1_p2, priority_encoder_1_p4,
       priority_encoder_1_p7;
  wire [2:0] priority_encoder_1_p5;
  wire [3:0] multiplexer_1_out;

  and and_1 (and_1_out, AluOPCon, nor_1_out);
  nor nor_1 (nor_1_out, Func[5], Func[4]);
  Multiplexer #(.width(4)) multiplexer_1 (.in0(ALUOP), .in1(Func[3:0]), .out(multiplexer_1_out), .sel(AluOPCon));
  and and_2 (and_2_out, ~multiplexer_1_out[3], ~multiplexer_1_out[2], ~multiplexer_1_out[1], ~multiplexer_1_out[0]);  // AND_Gate
  and and_3 (and_3_out, ~multiplexer_1_out[3], ~multiplexer_1_out[2], multiplexer_1_out[1], ~multiplexer_1_out[0]);  // AND_Gate
  and and_4 (and_4_out, ~multiplexer_1_out[3], multiplexer_1_out[2], ~multiplexer_1_out[1], ~multiplexer_1_out[0]);  // AND_Gate
  // Priority_Encoder #(.select(4)) priority_encoder_1: pin names not known; wires that end beside it: and_4_out, priority_encoder_1_p2, and_2_out, priority_encoder_1_p4, {Sub, priority_encoder_1_p5}, and_3_out, priority_encoder_1_p7
  and and_5 (priority_encoder_1_p2, ~multiplexer_1_out[3], multiplexer_1_out[2], ~multiplexer_1_out[1], multiplexer_1_out[0]);  // AND_Gate
  and and_6 (priority_encoder_1_p7, multiplexer_1_out[3], ~multiplexer_1_out[2], multiplexer_1_out[1], ~multiplexer_1_out[0]);  // AND_Gate
  and and_7 (priority_encoder_1_p4, ~multiplexer_1_out[3], multiplexer_1_out[2], multiplexer_1_out[1], ~multiplexer_1_out[0]);  // AND_Gate
  Multiplexer #(.width(3)) multiplexer_2 (.in0(priority_encoder_1_p5), .in1(Func[2:0]), .out(Op), .sel(and_1_out));

  // Notes on the sheet:
  //   Add
  //   Sub
  //   And
  //   Or
  //   Slt
  //   Xor
endmodule

module ControlUnit (
  input  [5:0] Op,
  input  [5:0] func,
  output RegDest,
  output Jump,
  output Branch,
  output BranchNE,
  output MemRead,
  output MemToReg,
  output MemWrite,
  output AlUSrc,
  output RegWrite,
  output AluOpCon,
  output [3:0] AluOp,
  output jalr,
  output ShiftCo,
  output jr
);

  wire ADDI_out, and_1_out, and_2_out, nor_1_out, or_1_out, or_2_out, priority_encoder_1_p3,
       priority_encoder_1_p4, priority_encoder_1_p5, priority_encoder_1_p7;

  and R (AluOpCon, ~Op[5], ~Op[4], ~Op[3], ~Op[2], ~Op[1], ~Op[0]);  // AND_Gate
  and LW (MemRead, Op[5], ~Op[4], ~Op[3], ~Op[2], Op[1], Op[0]);  // AND_Gate
  nor nor_1 (nor_1_out, func[5], func[4]);
  and SW (MemWrite, Op[5], ~Op[4], Op[3], ~Op[2], Op[1], Op[0]);  // AND_Gate
  and and_1 (and_1_out, func[0], ~func[1], ~func[2], func[3], ~func[4], ~func[5]);  // AND_Gate
  and and_2 (and_2_out, ~func[0], ~func[1], ~func[2], func[3], ~func[4], ~func[5]);  // AND_Gate
  and BEQ (Branch, ~Op[5], ~Op[4], ~Op[3], Op[2], ~Op[1], ~Op[0]);  // AND_Gate
  and and_3 (ShiftCo, AluOpCon, nor_1_out);
  and J (Jump, ~Op[5], ~Op[4], ~Op[3], ~Op[2], Op[1], ~Op[0]);  // AND_Gate
  or or_1 (or_1_out, MemRead, MemWrite, ADDI_out);
  and and_4 (jalr, and_1_out, AluOpCon);
  and and_5 (jr, and_2_out, AluOpCon);
  or or_2 (or_2_out, BranchNE, Branch);
  and BNE (BranchNE, ~Op[5], ~Op[4], ~Op[3], Op[2], ~Op[1], Op[0]);  // AND_Gate
  // Priority_Encoder #(.select(4)) priority_encoder_1: pin names not known; wires that end beside it: or_1_out, or_2_out, priority_encoder_1_p3, priority_encoder_1_p4, priority_encoder_1_p5, AluOp, priority_encoder_1_p7
  and ADDI (ADDI_out, ~Op[5], ~Op[4], Op[3], ~Op[2], ~Op[1], ~Op[0]);  // AND_Gate
  and ANDI (priority_encoder_1_p3, ~Op[5], ~Op[4], Op[3], Op[2], ~Op[1], ~Op[0]);  // AND_Gate
  and ORI (priority_encoder_1_p4, ~Op[5], ~Op[4], Op[3], Op[2], ~Op[1], Op[0]);  // AND_Gate
  and XORi (priority_encoder_1_p5, ~Op[5], ~Op[4], Op[3], Op[2], Op[1], ~Op[0]);  // AND_Gate
  and SLTI (priority_encoder_1_p7, ~Op[5], ~Op[4], Op[3], ~Op[2], Op[1], ~Op[0]);  // AND_Gate
  or or_3 (RegWrite, AluOpCon, MemRead, ADDI_out, priority_encoder_1_p3, priority_encoder_1_p4, priority_encoder_1_p5, priority_encoder_1_p7);
  or or_4 (AlUSrc, MemWrite, MemRead, ADDI_out, priority_encoder_1_p3, priority_encoder_1_p4, priority_encoder_1_p5, priority_encoder_1_p7);

  assign MemToReg = MemRead;
  assign RegDest = AluOpCon;
endmodule

module PC_Control (
  input  Jr,
  input  [25:0] Branch26,
  input  [31:0] OldPC,
  input  [31:0] Immediate,
  input  Jump,
  input  Branch,
  input  BranchNE,
  input  jalr,
  input  [31:0] BusA,
  input  ZeroFlag,
  output [31:0] NewPC,
  output [31:0] PC4
);

  wire and_1_out, and_2_out, or_1_out;
  wire [27:0] bit_extender_1_out, shifter_1_out;
  wire [31:0] adder_2_out, multiplexer_2_out, multiplexer_3_out, multiplexer_4_out, shifter_2_out;

  Adder #(.width(32)) adder_1 (.a(OldPC), .b(32'h4), .out(PC4));  // open: cin, cout
  assign bit_extender_1_out = {{2{1'b0}}, Branch26};  // Bit_Extender bit_extender_1
  Shifter #(.width(28)) shifter_1 (.in(bit_extender_1_out), .\dist (5'b00010), .out(shifter_1_out));
  Multiplexer #(.width(32)) multiplexer_1 (.in0(multiplexer_4_out), .in1(BusA), .out(NewPC), .sel(Jr));
  Shifter #(.width(32)) shifter_2 (.in(Immediate), .\dist (5'b00010), .out(shifter_2_out));
  Adder #(.width(32)) adder_2 (.a(PC4), .b(shifter_2_out), .out(adder_2_out));  // open: cin, cout
  and and_1 (and_1_out, Branch, ZeroFlag);
  and and_2 (and_2_out, BranchNE, ~ZeroFlag);  // AND_Gate
  Multiplexer #(.width(32)) multiplexer_2 (.in0(PC4), .in1(adder_2_out), .out(multiplexer_2_out), .sel(or_1_out));
  or or_1 (or_1_out, and_1_out, and_2_out);
  Multiplexer #(.width(32)) multiplexer_3 (
    .in0(multiplexer_2_out), .in1({PC4[31:28], shifter_1_out}), .out(multiplexer_3_out), .sel(Jump));
  Multiplexer #(.width(32)) multiplexer_4 (.in0(multiplexer_3_out), .in1(BusA), .out(multiplexer_4_out), .sel(jalr));
endmodule
